// Logisim project 4-bit_shift_add_3.circ as structural Verilog: 1 circuit, main circuit main
module main (
  input  A,
  input  B,
  input  C,
  input  D,
  input  A_2,
  input  B_2,
  input  C_2,
  input  D_2,
  output out_9,
  output out_10,
  output out_11,
  output out_12,
  output out_13,
  output out_14,
  output out_15,
  output out_16
);

  wire _1_2_out, _1_out, _2_2_out, _2_out, _3_2_out, _3_out, _4_2_out, _4_out, _5_2_out, _5_out, _6_2_out,
       _6_out, _7_2_out, _7_out, _8_2_out, _8_out, _9_2_out, _9_out, _11_2_out, _11_out, _12_2_out, _12_out,
       _13_2_out, _13_out, _15_2_out, _15_out, _17_2_out, _17_out, not_1_out, not_2_out, not_3_out,
       not_4_out, not_5_out, not_6_out;

  not _1 (_1_out, A_2);
  not _2 (_2_out, B_2);
  not _3 (_3_out, C_2);
  not _4 (_4_out, D_2);
  not _1_2 (_1_2_out, A);
  not _2_2 (_2_2_out, B);
  and _7 (_7_out, B, C);
  and _13 (_13_out, A, D);
  not _4_2 (_4_2_out, D);
  not _3_2 (_3_2_out, C);
  and _7_2 (_7_2_out, _1_out, D_2, _2_out);
  and _6 (_6_out, B_2, C_2);
  and _5 (_5_out, B_2, _3_out, _4_out);
  or _8 (_8_out, A_2, _6_out);
  and _6_2 (_6_2_out, _1_2_out, D, _2_2_out);
  or _11 (_11_out, _2_2_out, D);
  or _8_2 (_8_2_out, A, _7_out);
  and _15 (_15_out, A, _4_2_out);
  and _5_2 (_5_2_out, B, _4_2_out, _3_2_out);
  not not_1 (not_1_out, _8_out);
  not not_2 (not_2_out, _8_2_out);
  or _9 (_9_out, not_1_out, D_2);
  not not_3 (not_3_out, _9_out);
  and _12 (_12_out, _11_out, C);
  or _14 (out_10, _13_out, _5_2_out);
  or _9_2 (_9_2_out, not_2_out, D);
  or _10 (out_16, _7_2_out, not_3_out);
  not not_4 (not_4_out, _9_2_out);
  and _11_2 (_11_2_out, A_2, _4_out);
  not not_5 (not_5_out, _17_out);
  or _17 (_17_out, _2_2_out, out_10);
  or _16 (out_11, _12_out, _15_out);
  or _10_2 (out_12, _6_2_out, not_4_out);
  or _12_2 (_12_2_out, _2_out, D_2);
  and _13_2 (_13_2_out, _12_2_out, C_2);
  or _18 (out_9, A, not_5_out);
  or _14_2 (out_15, _13_2_out, _11_2_out);
  and _15_2 (_15_2_out, A_2, D_2);
  or _16_2 (out_14, _15_2_out, _5_out);
  not not_6 (not_6_out, _17_2_out);
  or _17_2 (_17_2_out, _2_out, out_14);
  or _18_2 (out_13, A_2, not_6_out);
endmodule
